# Fritzing sketch Schematic (saved by Fritzing 0.9.3b)
breadboards: 1

parts:
  U1 = EDISON
  S1 = Pushbutton [package="[THT]"]
  Part1 = ws2812b [package="smd 2812b"]
  R1 = Resistor [tolerance=±5% resistance=220 package=THT]
  J1 = Power Jack [package=power_jack_smd]

nets:
  VIN: U1.VIN, J1.GND, J1.GNDBREAK
  N1: U1.GP12_PWM0, S1.Pin_3, S1.Pin_4
  N2: U1.V_VSYS, Part1.VDD
  N3: U1.GP15, Part1.DIN
  GND: U1.GND, Part1.VSS, R1.Pin_1, J1.PWR
  N4: S1.Pin_1, S1.Pin_2, R1.Pin_0
